# Fritzing sketch rtc (saved by Fritzing 0.9.10b)
breadboards: 1

parts:
  V1 = DC Power [voltage=5]
  ZS-042_RTC1 = ZS-042 RTC Module  # not connected
  Mod1 = Amica NodeMCU DEVKIT 1.0

nets:
  N1: V1.V-, Mod1.pin2, Mod1.pin_9, Mod1.pin_25, Mod1.pin_29
  N2: Mod1.pin1, Mod1.pin_10, Mod1.pin_26
